// Logisim project 4BitCounter.circ as structural Verilog: 1 circuit, main circuit main
module main (
);

  wire and_1_out, and_2_out, and_3_out, button_1_out, j_k_ff_1_q, j_k_ff_2_q, j_k_ff_3_q, j_k_ff_4_q;

  and and_1 (and_1_out, and_3_out, j_k_ff_2_q);
  and and_2 (and_2_out, and_1_out, j_k_ff_3_q);
  Button button_1 (.out(button_1_out));
  and and_3 (and_3_out, 1'b1, j_k_ff_1_q);
  J_K_Flip_Flop j_k_ff_1 (.J(1'b1), .clk(button_1_out), .K(1'b1), .Q(j_k_ff_1_q));  // open: Qn, preset, en, reset
  J_K_Flip_Flop j_k_ff_2 (
    .J(and_3_out), .clk(button_1_out), .K(and_3_out), .Q(j_k_ff_2_q));  // open: Qn, preset, en, reset
  J_K_Flip_Flop j_k_ff_3 (
    .J(and_1_out), .clk(button_1_out), .K(and_1_out), .Q(j_k_ff_3_q));  // open: Qn, preset, en, reset
  J_K_Flip_Flop j_k_ff_4 (
    .J(and_2_out), .clk(button_1_out), .K(and_2_out), .Q(j_k_ff_4_q));  // open: Qn, preset, en, reset
  // NOT_Gate not_1 has open pins: in=j_k_ff_1_q, out=open
  LED led_1 (.in(j_k_ff_1_q));
  // NOT_Gate not_2 has open pins: in=j_k_ff_2_q, out=open
  LED led_2 (.in(j_k_ff_2_q));
  // NOT_Gate not_3 has open pins: in=j_k_ff_3_q, out=open
  LED led_3 (.in(j_k_ff_3_q));
  // NOT_Gate not_4 has open pins: in=j_k_ff_4_q, out=open
  LED led_4 (.in(j_k_ff_4_q));
endmodule
