// Logisim project Flipflops.circ as structural Verilog: 3 circuits, main circuit Gated SR Latch
module Gated_SR_Latch (
  input  S,
  input  R,
  output Q_prime,
  output Q
);

  wire and_1_out, and_2_out, button_1_out;

  Button button_1 (.out(button_1_out));
  and and_1 (and_1_out, S, button_1_out);
  and and_2 (and_2_out, button_1_out, R);
  nor nor_1 (Q_prime, and_1_out, Q);
  nor nor_2 (Q, Q_prime, and_2_out);
endmodule

module Gated_JK_Flipflop (
  input  J,
  input  K,
  output Q_prime,
  output Q
);

  wire and_1_out, and_2_out, button_1_out, register_1_q, register_2_q;

  Button button_1 (.out(button_1_out));
  and and_1 (and_1_out, Q_prime, J);
  and and_2 (and_2_out, K, Q);
  Register #(.width(1)) register_1 (.D(and_1_out), .en(1'b1), .Q(register_1_q), .clk(button_1_out));  // open: clr
  Register #(.width(1)) register_2 (.D(and_2_out), .en(1'b1), .Q(register_2_q), .clk(button_1_out));  // open: clr
  nor nor_1 (Q_prime, register_1_q, Q);
  nor nor_2 (Q, Q_prime, register_2_q);
endmodule

module Gated_D_Flipflop (
  input  D,
  output Q_prime,
  output Q
);

  wire and_1_out, and_2_out, button_1_out, not_1_out;

  Button button_1 (.out(button_1_out));
  not not_1 (not_1_out, D);
  and and_1 (and_1_out, D, button_1_out);
  and and_2 (and_2_out, button_1_out, not_1_out);
  nor nor_1 (Q_prime, and_1_out, Q);
  nor nor_2 (Q, Q_prime, and_2_out);
endmodule
