// Logisim project hwk2.circ as structural Verilog: 1 circuit, main circuit main
module main (
  input  X,
  input  in_2,
  input  Y,
  input  in_4,
  input  X_2,
  input  in_6,
  input  Y_2,
  input  in_8,
  input  X_3,
  input  X_4,
  output out_11,
  output out_12,
  output out_13,
  output out_14,
  output out_15,
  output out_16
);

  wire X_prime_4_out, X_prime_out, X_Y__prime_out, XY__prime_out, Y_prime_2_out, Y_prime_out;

  nand XY__prime (XY__prime_out, X, Y);
  nor X_prime (X_prime_out, X_2, X_2);
  nor Y_prime (Y_prime_out, Y_2, Y_2);
  nand XY__prime_prime (out_11, XY__prime_out, XY__prime_out);
  nor XY (out_13, X_prime_out, Y_prime_out);
  LED led_1 (.in(out_11));
  LED led_2 (.in(out_13));
  nand X_prime_2 (out_15, X_3, X_3);
  nor X_prime_3 (out_16, X_4, X_4);
  LED led_3 (.in(out_15));
  LED led_4 (.in(out_16));
  nand X_prime_4 (X_prime_4_out, in_2, in_2);
  nand Y_prime_2 (Y_prime_2_out, in_4, in_4);
  nor X_Y__prime (X_Y__prime_out, in_6, in_8);
  nand X_Y (out_12, X_prime_4_out, Y_prime_2_out);
  nor X_Y_2 (out_14, X_Y__prime_out, X_Y__prime_out);
  LED led_5 (.in(out_12));
  LED led_6 (.in(out_14));

  // Notes on the sheet:
  //   AND Circuit Using NAND & NOR Gates
  //   NOT Circuit Using NAND & NOR Gates
  //   OR Circuit Using NAND & NOR Gates
endmodule
