// Logisim project in_class126.circ as structural Verilog: 1 circuit, main circuit main
module main (
  input  X,
  input  Y,
  input  Z,
  input  A,
  input  B,
  output W,
  output C
);

  wire nand_1_out, nand_2_out, undriven, Y_prime_Z_out;

  // NOT_Gate not_1 has open pins: in=Y, out=open
  Adder adder_1 ();  // open: a, b, out, cin, cout
  nand nand_1 (nand_1_out, A, A);
  nand nand_2 (nand_2_out, B, B);
  // AND_Gate Y_prime_Z has open pins: out=Y_prime_Z_out
  not nand_3 (C, nand_2_out);  // NAND_Gate
  or X_Y_prime_Z (W, undriven, Y_prime_Z_out);
endmodule
