// Logisim project project1.circ as structural Verilog: 1 circuit, main circuit main
module main (
  input  X,
  input  X_2,
  input  Y,
  input  Y_2,
  input  Y_3,
  input  X_3,
  output out_7,
  output out_8,
  output out_9,
  output out_10
);

  wire C_out_3_out, C_out_out, not_1_out, not_2_out, not_3_out, not_4_out, not_5_out, not_6_out, not_7_out,
       not_8_out, not_9_out, not_10_out, not_11_out, not_12_out, not_13_out, not_14_out, not_16_out,
       not_17_out, not_18_out, X_prime_Y_prime_C_in_2_out, X_prime_Y_prime_C_in_3_out,
       X_prime_Y_prime_C_in_out, X_prime_YC_in_prime_2_out, X_prime_YC_in_prime_3_out,
       X_prime_YC_in_prime_out, XC_in_2_out, XC_in_3_out, XC_in_out, XY_2_out, XY_3_out, XY_out,
       XY_prime_C_in_prime_2_out, XY_prime_C_in_prime_3_out, XY_prime_C_in_prime_out, XYC_in_2_out,
       XYC_in_3_out, XYC_in_out, YC_in_2_out, YC_in_3_out, YC_in_out;

  not not_1 (not_1_out, X);
  not not_2 (not_2_out, Y);
  not not_3 (not_3_out, X);
  not not_4 (not_4_out, 1'b0);
  not not_5 (not_5_out, Y);
  not not_6 (not_6_out, 1'b0);
  and X_prime_Y_prime_C_in (X_prime_Y_prime_C_in_out, not_1_out, not_2_out, 1'b0);
  and X_prime_YC_in_prime (X_prime_YC_in_prime_out, not_3_out, Y, not_4_out);
  and XY_prime_C_in_prime (XY_prime_C_in_prime_out, X, not_5_out, not_6_out);
  and XYC_in (XYC_in_out, X, Y, 1'b0);
  and XY (XY_out, Y, X);
  and XC_in (XC_in_out, 1'b0, X);
  and YC_in (YC_in_out, 1'b0, Y);
  or Sum (out_7, X_prime_Y_prime_C_in_out, X_prime_YC_in_prime_out, XY_prime_C_in_prime_out, XYC_in_out);
  or C_out (C_out_out, XY_out, XC_in_out, YC_in_out);
  LED led_1 (.in(out_7));
  and YC_in_2 (YC_in_2_out, C_out_3_out, Y_3);
  not not_7 (not_7_out, X_2);
  not not_8 (not_8_out, Y_2);
  not not_9 (not_9_out, X_2);
  not not_10 (not_10_out, C_out_out);
  not not_11 (not_11_out, Y_2);
  not not_12 (not_12_out, C_out_out);
  and XC_in_2 (XC_in_2_out, C_out_3_out, X_3);
  or C_out_2 (out_9, YC_in_2_out, XC_in_2_out, XY_3_out);
  and X_prime_Y_prime_C_in_2 (X_prime_Y_prime_C_in_2_out, not_7_out, not_8_out, C_out_out);
  and X_prime_YC_in_prime_2 (X_prime_YC_in_prime_2_out, not_9_out, Y_2, not_10_out);
  and XY_prime_C_in_prime_2 (XY_prime_C_in_prime_2_out, X_2, not_11_out, not_12_out);
  and XYC_in_2 (XYC_in_2_out, X_2, Y_2, C_out_out);
  and XY_2 (XY_2_out, Y_2, X_2);
  and XC_in_3 (XC_in_3_out, C_out_out, X_2);
  and YC_in_3 (YC_in_3_out, C_out_out, Y_2);
  and XY_3 (XY_3_out, Y_3, X_3);
  LED led_2 (.in(out_9));
  not not_13 (not_13_out, Y_3);
  not not_14 (not_14_out, C_out_3_out);
  and XYC_in_3 (XYC_in_3_out, C_out_3_out, Y_3, X_3);
  and XY_prime_C_in_prime_3 (XY_prime_C_in_prime_3_out, not_14_out, not_13_out, X_3);
  LED led_3 (.in(out_10));
  or Sum_2 (out_8, X_prime_Y_prime_C_in_2_out, X_prime_YC_in_prime_2_out, XY_prime_C_in_prime_2_out, XYC_in_2_out);
  LED led_4 (.in(out_8));
  or C_out_3 (C_out_3_out, XY_2_out, XC_in_3_out, YC_in_3_out);
  // NOT_Gate not_15 has open pins: in=X_3, out=open
  not not_16 (not_16_out, C_out_3_out);
  and X_prime_YC_in_prime_3 (X_prime_YC_in_prime_3_out, not_16_out, Y_3);
  or Sum_3 (out_10, XYC_in_3_out, XY_prime_C_in_prime_3_out, X_prime_YC_in_prime_3_out, X_prime_Y_prime_C_in_3_out);
  not not_17 (not_17_out, Y_3);
  not not_18 (not_18_out, X_3);
  and X_prime_Y_prime_C_in_3 (X_prime_Y_prime_C_in_3_out, C_out_3_out, not_17_out, not_18_out);
endmodule
