// Logisim project project2.circ as structural Verilog: 8 circuits, main circuit main
module main (
);

  wire BC_out_2, BL_out_2, BR_out_2, button_1_out, C_out_2, TC_out_2, TL_out_2, TR_out_2;

  Button button_1 (.out(button_1_out));
  TopCenter TC (.in_1(button_1_out), .out_2(TC_out_2));
  TopRight TR (.in_1(button_1_out), .out_2(TR_out_2));
  TopLeft TL (.in_1(button_1_out), .out_2(TL_out_2));
  BottomLeft BL (.in_1(button_1_out), .out_2(BL_out_2));
  Center C (.in_1(button_1_out), .out_2(C_out_2));
  BottomCenter BC (.in_1(button_1_out), .out_2(BC_out_2));
  _7_Segment_Display u_7_segment_display_1 (
    .g(C_out_2), .f(TL_out_2), .a(TC_out_2), .b(TR_out_2), .e(BL_out_2), .d(BC_out_2), .c(BR_out_2));  // open: dp
  BottomRight BR (.in_1(button_1_out), .out_2(BR_out_2));
endmodule

module TopCenter (
  input  in_1,
  output out_2
);

  wire and_1_out, and_2_out, and_3_out, not_1_out, not_2_out, not_3_out, not_4_out, x0_q, x1_q,
       x2_prime_x1_prime_x0_prime_out, x2_q, x3_prime_x1_out, x3_prime_x2x0_out, x3_q,
       x3x2_prime_x1_prime_out, x3x2_prime_x1x0_prime_out;

  and and_1 (and_1_out, and_3_out, x1_q);
  and and_2 (and_2_out, and_1_out, x2_q);
  and and_3 (and_3_out, 1'b1, x0_q);
  J_K_Flip_Flop x0 (
    .J(1'b1), .clk(in_1), .K(1'b1), .Q(x0_q), .reset(x3x2_prime_x1x0_prime_out));  // open: Qn, preset, en
  J_K_Flip_Flop x1 (
    .J(and_3_out), .clk(in_1), .K(and_3_out), .Q(x1_q), .reset(x3x2_prime_x1x0_prime_out));  // open: Qn, preset, en
  J_K_Flip_Flop x2 (
    .J(and_1_out), .clk(in_1), .K(and_1_out), .Q(x2_q), .reset(x3x2_prime_x1x0_prime_out));  // open: Qn, preset, en
  J_K_Flip_Flop x3 (
    .J(and_2_out), .clk(in_1), .K(and_2_out), .Q(x3_q), .reset(x3x2_prime_x1x0_prime_out));  // open: Qn, preset, en
  and x3x2_prime_x1x0_prime (x3x2_prime_x1x0_prime_out, not_1_out, x1_q, not_3_out, x3_q);
  not not_1 (not_1_out, x0_q);
  not not_2 (not_2_out, x1_q);
  not not_3 (not_3_out, x2_q);
  not not_4 (not_4_out, x3_q);
  and x3x2_prime_x1_prime (x3x2_prime_x1_prime_out, not_2_out, not_3_out, x3_q);
  and x3_prime_x2x0 (x3_prime_x2x0_out, x0_q, x2_q, not_4_out);
  and x3_prime_x1 (x3_prime_x1_out, x1_q, not_4_out);
  or or_1 (out_2, x3x2_prime_x1_prime_out, x3_prime_x2x0_out, x3_prime_x1_out, x2_prime_x1_prime_x0_prime_out);
  and x2_prime_x1_prime_x0_prime (x2_prime_x1_prime_x0_prime_out, not_1_out, not_2_out, not_3_out);
endmodule

module TopRight (
  input  in_1,
  output out_2
);

  wire and_1_out, and_2_out, and_3_out, not_1_out, not_2_out, not_3_out, not_4_out, x0_q, x1_q,
       x2_prime_x1_prime_out, x2_q, x3_prime_x1_prime_x0_prime_out, x3_prime_x1x0_out, x3_prime_x2_prime_out,
       x3_q, x3x2_prime_x1x0_prime_out;

  and and_1 (and_1_out, and_3_out, x1_q);
  and and_2 (and_2_out, and_1_out, x2_q);
  and and_3 (and_3_out, 1'b1, x0_q);
  J_K_Flip_Flop x0 (
    .J(1'b1), .clk(in_1), .K(1'b1), .Q(x0_q), .reset(x3x2_prime_x1x0_prime_out));  // open: Qn, preset, en
  J_K_Flip_Flop x1 (
    .J(and_3_out), .clk(in_1), .K(and_3_out), .Q(x1_q), .reset(x3x2_prime_x1x0_prime_out));  // open: Qn, preset, en
  J_K_Flip_Flop x2 (
    .J(and_1_out), .clk(in_1), .K(and_1_out), .Q(x2_q), .reset(x3x2_prime_x1x0_prime_out));  // open: Qn, preset, en
  J_K_Flip_Flop x3 (
    .J(and_2_out), .clk(in_1), .K(and_2_out), .Q(x3_q), .reset(x3x2_prime_x1x0_prime_out));  // open: Qn, preset, en
  not not_1 (not_1_out, x0_q);
  not not_2 (not_2_out, x1_q);
  not not_3 (not_3_out, x2_q);
  not not_4 (not_4_out, x3_q);
  and x3x2_prime_x1x0_prime (x3x2_prime_x1x0_prime_out, not_1_out, x1_q, not_3_out, x3_q);
  and x3_prime_x2_prime (x3_prime_x2_prime_out, not_4_out, not_3_out);
  and x3_prime_x1_prime_x0_prime (x3_prime_x1_prime_x0_prime_out, not_4_out, not_2_out, not_1_out);
  and x3_prime_x1x0 (x3_prime_x1x0_out, not_4_out, x1_q, x0_q);
  and x2_prime_x1_prime (x2_prime_x1_prime_out, not_3_out, not_2_out);
  or or_1 (out_2, x3_prime_x2_prime_out, x3_prime_x1_prime_x0_prime_out, x3_prime_x1x0_out, x2_prime_x1_prime_out);
endmodule

module BottomRight (
  input  in_1,
  output out_2
);

  wire and_1_out, and_2_out, and_3_out, not_1_out, not_2_out, not_3_out, not_4_out, x0_q, x1_q, x2_q,
       x3_prime_x1x0_out, x3_prime_x2_out, x3_prime_x2_prime_x1_prime_out, x3_q, x3x2_prime_x1_prime_out,
       x3x2_prime_x1x0_prime_out;

  and and_1 (and_1_out, and_3_out, x1_q);
  and and_2 (and_2_out, and_1_out, x2_q);
  and and_3 (and_3_out, 1'b1, x0_q);
  J_K_Flip_Flop x0 (
    .J(1'b1), .clk(in_1), .K(1'b1), .Q(x0_q), .reset(x3x2_prime_x1x0_prime_out));  // open: Qn, preset, en
  J_K_Flip_Flop x1 (
    .J(and_3_out), .clk(in_1), .K(and_3_out), .Q(x1_q), .reset(x3x2_prime_x1x0_prime_out));  // open: Qn, preset, en
  J_K_Flip_Flop x2 (
    .J(and_1_out), .clk(in_1), .K(and_1_out), .Q(x2_q), .reset(x3x2_prime_x1x0_prime_out));  // open: Qn, preset, en
  J_K_Flip_Flop x3 (
    .J(and_2_out), .clk(in_1), .K(and_2_out), .Q(x3_q), .reset(x3x2_prime_x1x0_prime_out));  // open: Qn, preset, en
  not not_1 (not_1_out, x0_q);
  not not_2 (not_2_out, x1_q);
  not not_3 (not_3_out, x2_q);
  not not_4 (not_4_out, x3_q);
  and x3x2_prime_x1x0_prime (x3x2_prime_x1x0_prime_out, not_1_out, x1_q, not_3_out, x3_q);
  and x3_prime_x2_prime_x1_prime (x3_prime_x2_prime_x1_prime_out, not_4_out, not_3_out, not_2_out);
  and x3_prime_x1x0 (x3_prime_x1x0_out, not_4_out, x1_q, x0_q);
  and x3_prime_x2 (x3_prime_x2_out, not_4_out, x2_q);
  and x3x2_prime_x1_prime (x3x2_prime_x1_prime_out, x3_q, not_3_out, not_2_out);
  or or_1 (out_2, x3_prime_x2_prime_x1_prime_out, x3_prime_x1x0_out, x3_prime_x2_out, x3x2_prime_x1_prime_out);
endmodule

module BottomCenter (
  input  in_1,
  output out_2
);

  wire and_1_out, and_2_out, and_3_out, not_1_out, not_2_out, not_3_out, not_4_out, x0_q, x1_q,
       x2_prime_x1_prime_x0_prime_out, x2_q, x3_prime_x1x0_prime_out, x3_prime_x2_prime_x1_out,
       x3_prime_x2x1_prime_x0_out, x3_q, x3x2_prime_x1_prime_out, x3x2_prime_x1x0_prime_out;

  and and_1 (and_1_out, and_3_out, x1_q);
  and and_2 (and_2_out, and_1_out, x2_q);
  and and_3 (and_3_out, 1'b1, x0_q);
  J_K_Flip_Flop x0 (
    .J(1'b1), .clk(in_1), .K(1'b1), .Q(x0_q), .reset(x3x2_prime_x1x0_prime_out));  // open: Qn, preset, en
  J_K_Flip_Flop x1 (
    .J(and_3_out), .clk(in_1), .K(and_3_out), .Q(x1_q), .reset(x3x2_prime_x1x0_prime_out));  // open: Qn, preset, en
  J_K_Flip_Flop x2 (
    .J(and_1_out), .clk(in_1), .K(and_1_out), .Q(x2_q), .reset(x3x2_prime_x1x0_prime_out));  // open: Qn, preset, en
  J_K_Flip_Flop x3 (
    .J(and_2_out), .clk(in_1), .K(and_2_out), .Q(x3_q), .reset(x3x2_prime_x1x0_prime_out));  // open: Qn, preset, en
  not not_1 (not_1_out, x0_q);
  not not_2 (not_2_out, x1_q);
  not not_3 (not_3_out, x2_q);
  not not_4 (not_4_out, x3_q);
  and x3x2_prime_x1x0_prime (x3x2_prime_x1x0_prime_out, not_1_out, x1_q, not_3_out, x3_q);
  and x2_prime_x1_prime_x0_prime (x2_prime_x1_prime_x0_prime_out, not_3_out, not_2_out, not_1_out);
  and x3_prime_x2_prime_x1 (x3_prime_x2_prime_x1_out, not_4_out, not_3_out, x1_q);
  and x3_prime_x1x0_prime (x3_prime_x1x0_prime_out, not_4_out, x1_q, not_1_out);
  and x3_prime_x2x1_prime_x0 (x3_prime_x2x1_prime_x0_out, not_4_out, x2_q, not_2_out, x0_q);
  and x3x2_prime_x1_prime (x3x2_prime_x1_prime_out, x3_q, not_3_out, not_2_out);
  or or_1 (out_2, x2_prime_x1_prime_x0_prime_out, x3_prime_x2_prime_x1_out, x3_prime_x1x0_prime_out, x3_prime_x2x1_prime_x0_out, x3x2_prime_x1_prime_out);
endmodule

module BottomLeft (
  input  in_1,
  output out_2
);

  wire and_1_out, and_2_out, and_3_out, not_1_out, not_2_out, not_3_out, not_4_out, x0_q, x1_q,
       x2_prime_x1_prime_x0_prime_out, x2_q, x3_prime_x1x0_prime_out, x3_q, x3x2_prime_x1x0_prime_out;

  and and_1 (and_1_out, and_3_out, x1_q);
  and and_2 (and_2_out, and_1_out, x2_q);
  and and_3 (and_3_out, 1'b1, x0_q);
  J_K_Flip_Flop x0 (
    .J(1'b1), .clk(in_1), .K(1'b1), .Q(x0_q), .reset(x3x2_prime_x1x0_prime_out));  // open: Qn, preset, en
  J_K_Flip_Flop x1 (
    .J(and_3_out), .clk(in_1), .K(and_3_out), .Q(x1_q), .reset(x3x2_prime_x1x0_prime_out));  // open: Qn, preset, en
  J_K_Flip_Flop x2 (
    .J(and_1_out), .clk(in_1), .K(and_1_out), .Q(x2_q), .reset(x3x2_prime_x1x0_prime_out));  // open: Qn, preset, en
  J_K_Flip_Flop x3 (
    .J(and_2_out), .clk(in_1), .K(and_2_out), .Q(x3_q), .reset(x3x2_prime_x1x0_prime_out));  // open: Qn, preset, en
  not not_1 (not_1_out, x0_q);
  not not_2 (not_2_out, x1_q);
  not not_3 (not_3_out, x2_q);
  not not_4 (not_4_out, x3_q);
  and x3x2_prime_x1x0_prime (x3x2_prime_x1x0_prime_out, not_1_out, x1_q, not_3_out, x3_q);
  and x2_prime_x1_prime_x0_prime (x2_prime_x1_prime_x0_prime_out, not_3_out, not_2_out, not_1_out);
  and x3_prime_x1x0_prime (x3_prime_x1x0_prime_out, not_4_out, x1_q, not_1_out);
  or or_1 (out_2, x2_prime_x1_prime_x0_prime_out, x3_prime_x1x0_prime_out);
endmodule

module TopLeft (
  input  in_1,
  output out_2
);

  wire and_1_out, and_2_out, and_3_out, not_1_out, not_2_out, not_3_out, not_4_out, x0_q, x1_q, x2_q,
       x3_prime_x1_prime_x0_prime_out, x3_prime_x2x0_prime_out, x3_prime_x2x1_prime_out, x3_q,
       x3x2_prime_x1_prime_out, x3x2_prime_x1x0_prime_out;

  and and_1 (and_1_out, and_3_out, x1_q);
  and and_2 (and_2_out, and_1_out, x2_q);
  and and_3 (and_3_out, 1'b1, x0_q);
  J_K_Flip_Flop x0 (
    .J(1'b1), .clk(in_1), .K(1'b1), .Q(x0_q), .reset(x3x2_prime_x1x0_prime_out));  // open: Qn, preset, en
  J_K_Flip_Flop x1 (
    .J(and_3_out), .clk(in_1), .K(and_3_out), .Q(x1_q), .reset(x3x2_prime_x1x0_prime_out));  // open: Qn, preset, en
  J_K_Flip_Flop x2 (
    .J(and_1_out), .clk(in_1), .K(and_1_out), .Q(x2_q), .reset(x3x2_prime_x1x0_prime_out));  // open: Qn, preset, en
  J_K_Flip_Flop x3 (
    .J(and_2_out), .clk(in_1), .K(and_2_out), .Q(x3_q), .reset(x3x2_prime_x1x0_prime_out));  // open: Qn, preset, en
  not not_1 (not_1_out, x0_q);
  not not_2 (not_2_out, x1_q);
  not not_3 (not_3_out, x2_q);
  not not_4 (not_4_out, x3_q);
  and x3x2_prime_x1x0_prime (x3x2_prime_x1x0_prime_out, not_1_out, x1_q, not_3_out, x3_q);
  and x3_prime_x1_prime_x0_prime (x3_prime_x1_prime_x0_prime_out, not_4_out, not_2_out, not_1_out);
  and x3_prime_x2x0_prime (x3_prime_x2x0_prime_out, not_4_out, x2_q, not_1_out);
  and x3_prime_x2x1_prime (x3_prime_x2x1_prime_out, not_4_out, x2_q, not_2_out);
  and x3x2_prime_x1_prime (x3x2_prime_x1_prime_out, x3_q, not_3_out, not_2_out);
  or or_1 (out_2, x3_prime_x1_prime_x0_prime_out, x3_prime_x2x0_prime_out, x3_prime_x2x1_prime_out, x3x2_prime_x1_prime_out);
endmodule

module Center (
  input  in_1,
  output out_2
);

  wire and_1_out, and_2_out, and_3_out, not_1_out, not_2_out, not_3_out, not_4_out, x0_q, x1_q, x2_q,
       x3_prime_x1x0_prime_out, x3_prime_x2_prime_x1_out, x3_prime_x2x1_prime_out, x3_q,
       x3x2_prime_x1_prime_out, x3x2_prime_x1x0_prime_out;

  and and_1 (and_1_out, and_3_out, x1_q);
  and and_2 (and_2_out, and_1_out, x2_q);
  and and_3 (and_3_out, 1'b1, x0_q);
  J_K_Flip_Flop x0 (
    .J(1'b1), .clk(in_1), .K(1'b1), .Q(x0_q), .reset(x3x2_prime_x1x0_prime_out));  // open: Qn, preset, en
  J_K_Flip_Flop x1 (
    .J(and_3_out), .clk(in_1), .K(and_3_out), .Q(x1_q), .reset(x3x2_prime_x1x0_prime_out));  // open: Qn, preset, en
  J_K_Flip_Flop x2 (
    .J(and_1_out), .clk(in_1), .K(and_1_out), .Q(x2_q), .reset(x3x2_prime_x1x0_prime_out));  // open: Qn, preset, en
  J_K_Flip_Flop x3 (
    .J(and_2_out), .clk(in_1), .K(and_2_out), .Q(x3_q), .reset(x3x2_prime_x1x0_prime_out));  // open: Qn, preset, en
  not not_1 (not_1_out, x0_q);
  not not_2 (not_2_out, x1_q);
  not not_3 (not_3_out, x2_q);
  not not_4 (not_4_out, x3_q);
  and x3x2_prime_x1x0_prime (x3x2_prime_x1x0_prime_out, not_1_out, x1_q, not_3_out, x3_q);
  and x3_prime_x2_prime_x1 (x3_prime_x2_prime_x1_out, not_4_out, not_3_out, x1_q);
  and x3_prime_x1x0_prime (x3_prime_x1x0_prime_out, not_4_out, x1_q, not_1_out);
  and x3_prime_x2x1_prime (x3_prime_x2x1_prime_out, not_4_out, x2_q, not_2_out);
  and x3x2_prime_x1_prime (x3x2_prime_x1_prime_out, x3_q, not_3_out, not_2_out);
  or or_1 (out_2, x3_prime_x2_prime_x1_out, x3_prime_x1x0_prime_out, x3_prime_x2x1_prime_out, x3x2_prime_x1_prime_out);
endmodule
